// Logisim project item_c.circ as structural Verilog: 1 circuit, main circuit main
module main (
  input  A,
  input  B,
  input  C,
  input  D,
  output X
);

  wire and_1_out, not_1_out, not_2_out, or_1_out;

  and and_1 (and_1_out, A, B);
  or or_1 (or_1_out, C, D);
  not not_1 (not_1_out, and_1_out);
  not not_2 (not_2_out, or_1_out);
  and and_2 (X, not_1_out, not_2_out);

  // Notes on the sheet:
  //   X=A'B'(C'+D')
endmodule
