// Logisim project item_d.circ as structural Verilog: 1 circuit, main circuit main
module main (
  input  A,
  input  B,
  input  C,
  input  A_2,
  input  B_2,
  input  C_2,
  output X,
  output Y
);

  wire and_1_out, and_2_out, and_3_out;

  and and_1 (and_1_out, A_2, B_2);
  and and_2 (and_2_out, B_2, C_2);
  and and_3 (and_3_out, C_2, A_2);
  ExactlyOne xor_1 (.out(X), .in0(A), .in1(B), .in2(C));
  or or_1 (Y, and_1_out, and_2_out, and_3_out);

  // Notes on the sheet:
  //   X:
  //   Y:
endmodule
