// Logisim project questao03.circ as structural Verilog: 1 circuit, main circuit main
module main (
  input  A,
  input  B,
  input  C,
  input  D,
  output X
);

  wire and_1_out, and_2_out, and_3_out, not_1_out, not_2_out, not_3_out;

  not not_1 (not_1_out, D);
  not not_2 (not_2_out, and_1_out);
  and and_1 (and_1_out, A, B);
  and and_2 (and_2_out, B, D);
  not not_3 (not_3_out, and_2_out);
  and and_3 (and_3_out, not_1_out, C, A);
  or or_1 (X, not_2_out, not_3_out, and_3_out);

  // Notes on the sheet:
  //   X=A'B'+B'D'+ACD'
endmodule
