// Logisim project questao04.circ as structural Verilog: 1 circuit, main circuit main
module main (
  input  T,
  input  H,
  input  F,
  input  U,
  output A
);

  wire and_1_out, and_2_out;

  and and_1 (and_1_out, T, H);
  and and_2 (and_2_out, F, U);
  or or_1 (A, and_1_out, and_2_out);
endmodule
