// Logisim project questao05.circ as structural Verilog: 1 circuit, main circuit main
module main (
  input  B2,
  input  B1,
  input  B2_2,
  input  B1_2,
  input  B2_3,
  input  B1_3,
  input  B0,
  output Y3,
  output Y2,
  output Y1
);

  wire and_3_out, and_4_out, not_1_out, not_2_out;

  not not_1 (not_1_out, B1_2);
  not not_2 (not_2_out, B2_3);
  and and_1 (Y3, B2, B1);
  and and_2 (Y2, B2_2, not_1_out);
  and and_3 (and_3_out, not_2_out, B1_3);
  and and_4 (and_4_out, B2_3, B0);
  or or_1 (Y1, and_3_out, and_4_out);

  // Notes on the sheet:
  //   Y3=B2B1
  //   Y2=B2B1'
  //   Y1=B2'B1+B2B0
  //   Y0=1
endmodule
